# Fritzing sketch Time_Bomb_Schematic (saved by Fritzing 0.9.5d)
breadboards: 1

parts:
  LCD1 = LCD screen
  R1 = Resistor [tolerance=±5% resistance=100 package=THT]
  Part1 = Arduino Uno (Rev3)
  J1 = Piezo Speaker
  LCM1602_IIC1 = LCM1602 IIC [part_number="LCM1602 IIC" chip_label="LCM1602 IIC" package="DIP (Dual Inline) [THT]"]
  S1 = Pushbutton [package="[THT]"]
  S2 = Pushbutton [package="[THT]"]
  S3 = Pushbutton [package="[THT]"]
  R2 = Resistor [tolerance=±5% resistance=1k package=THT]
  R3 = Resistor [tolerance=±5% resistance=1k package=THT]
  R4 = Resistor [tolerance=±5% resistance=1k package=THT]

nets:
  VSS: LCD1.VSS, LCM1602_IIC1.VSS
  VDD: LCD1.VDD, LCM1602_IIC1.VDD
  N1: LCD1.V0, LCM1602_IIC1.V0
  N2: LCD1.RS, LCM1602_IIC1.RS
  N3: LCD1.R/W, LCM1602_IIC1.RW
  N4: LCD1.E, LCM1602_IIC1.E
  N5: LCD1.DB0, LCM1602_IIC1.D0
  N6: LCD1.DB1, LCM1602_IIC1.D1
  N7: LCD1.DB2, LCM1602_IIC1.D2
  N8: LCD1.DB3, LCM1602_IIC1.D3
  N9: LCD1.DB4, LCM1602_IIC1.D4
  N10: LCD1.DB5, LCM1602_IIC1.D5
  N11: LCD1.DB6, LCM1602_IIC1.D6
  N12: LCD1.DB7, LCM1602_IIC1.D7
  N13: LCD1.LED+, LCM1602_IIC1.A
  N14: LCD1.LED-, LCM1602_IIC1.K
  N15: R1.Pin_0, J1.pin1
  GND: R1.Pin_1, Part1.GND, LCM1602_IIC1.GND, R2.Pin_1, R3.Pin_1, R4.Pin_1
  N16: Part1.A4/SDA, LCM1602_IIC1.SDA
  N17: Part1.A5/SCL, LCM1602_IIC1.SCL
  N18: Part1.D9_PWM, J1.pin2
  N19: Part1.D10_PWM/SS, S1.Pin_3, S1.Pin_4, R4.Pin_0
  N20: Part1.D11_PWM/MOSI, S2.Pin_3, S2.Pin_4, R3.Pin_0
  N21: Part1.D12/MISO, S3.Pin_3, S3.Pin_4, R2.Pin_0
  5V: Part1.5V, LCM1602_IIC1.VCC, S1.Pin_1, S1.Pin_2, S2.Pin_1, S2.Pin_2, S3.Pin_1, S3.Pin_2
  N22: LCM1602_IIC1.LED_A, LCM1602_IIC1.LED_B

custom parts:
  LCM1602 IIC: I2C-Module to use a 1602 or 2004 LCD on with the wire.h libory Serial LCD Modul

// code stored in the sketch: a_presetup.ino
#include <LiquidCrystal.h>;
#include <CountUpDownTimer.h>;
int buzzFreq = 100;
int BuzzerPin = 9;
const int rs = 12, en = 11, d4 = 5, d5 = 4, d6 = 3, d7 = 2;
LiquidCrystal lcd(rs, en, d4, d5, d6, d7);
CountUpDownTimer T(DOWN);

// code stored in the sketch: a_variables.ino


// code stored in the sketch: b_setup.ino
void setup() { 
    pinMode(BuzzerPin,OUTPUT);
    Serial.begin(115200);
    T.SetTimer(0,10,0); //H,M,S
    T.StartTimer();
    lcd.begin(16,2);  //col,row

    
}

// code stored in the sketch: c_loop.ino
void loop() {
  T.Timer();

  if (T.TimeHasChanged() ){
    
    Serial.print(T.ShowMinutes());
    Serial.print(":");
    Serial.println(T.ShowSeconds());
    tone(BuzzerPin, 3000);
    delay(100);
    noTone(BuzzerPin);
    delay(900);
    lcd.setCursor(0, 0); //col, row
    lcd.print("you have");
    lcd.print(T.ShowMinutes());
    lcd.print(":");
    lcd.print(T.ShowSeconds());
    lcd.print(" to");
    lcd.setCursor(0, 1);
    lcd.print("clear the area");
  }
    
}

// code stored in the sketch: Time_Bomb.ino
/*
 * Project by Panos Koutsoumanis
 * last edited on 16/11/2019
 * 
 * Parts required:
 *   17x cables
 *   1x 100Ω resistor
 *   1x 220Ω resistor
 *   1x 10kΩ potentiometer
 *   1x piezo buzzer
 *   1x Arduino UNO (or any arduino with pwm)
 * 
 * Wiring:
 *   it is strongly advised to draw the 5V and ground lines from the UNO to the breadboard, since the pins on board are not enough for every device.
 *   lcd pin VSS to 5V
 *   lcd pin VDD to ground
 *   lcd pin RS to digital pin 12
 *   lcd pin Enable (E) to digital pin 11
 *   lcd pin Dataline 4 (D4) to digital pin 5
 *   lcd pin Dataline 5 (D5) to digital pin 4
 *   lcd pin Dataline 6 (D6) to digital pin 3
 *   lcd pin Dataline 7 (D7) to digital pin 2
 *   lcd pin contrast Vin (A) through 220Ω res to 5V
 *   lcd pin contrast Gnd (K) to ground
 *   10K potentiometer:
 *     Sides to 5V and Gnd
 *     Wiper (middle pin) to lcd pin contrast (V0)
 *   Buzzer:
 *     Vin pin (+) to digital pin 9
 *     Gnd pin (-) through 100Ω resistor to ground
 * 
 * Code: a_presetup tab contains variables and library setups
 *       b_setup tab contains the void setup(); code
 *       c_lopp tab contains the void loop(); code
 *       
 *       
 *     
*/
